# Fritzing sketch Fritzing Circuit (saved by Fritzing 0.9.3b)

parts:
  LCD1 = LCD screen
  Part1 = Arduino Nano (Rev3.0)
  M1 = MakerFocus MAX30102
  U1 = POT_SWITCH [package=pot_pth]

nets:
  GND: LCD1.VSS, LCD1.R/W, LCD1.LED-, Part1.GND, M1.GND, U1.G$1_A
  VDD: LCD1.VDD, LCD1.LED+, Part1.5V, M1.VIN, U1.G$1_E
  N1: LCD1.V0, U1.G$2_1
  N2: LCD1.RS, Part1.D12/MISO
  N3: LCD1.E, Part1.D11/MOSI
  N4: LCD1.DB4, Part1.D5
  N5: LCD1.DB5, Part1.D4
  N6: LCD1.DB6, Part1.D3
  N7: LCD1.DB7, Part1.D2
  N8: Part1.A5, M1.SCL
  N9: Part1.A4, M1.SDA

custom parts:
  MakerFocus MAX30102: Oximeter module using the MAX30102 chip. As usual, if you want the mounting holes in pcb, you need to drag a hole over the pad in silkscreen to actually drill the hole (by default they are not drilled)
